# Fritzing sketch ESP32C3_VL6180 (saved by Fritzing 0.9.9b)
circuit board: 17.8118cm x 6.14559cm

parts:
  VL6180 = Adafruit VL6180X Time of Flight Distance Sensor [part_number="Adafruit #3316"]
  A1 = Esp32-c3 super mini

nets:
  N1: VL6180.VIN, A1.Pin_14
  N2: VL6180.GND, A1.Pin_15
  N3: VL6180.SCL, A1.Pin_3
  N4: VL6180.SDA, A1.Pin_2

custom parts:
  Adafruit VL6180X Time of Flight Distance Sensor: The VL6180X is a Time of Flight distance sensor like no other you've used! The sensor contains a very tiny invisible laser source, and a matching sensor. The VL6180X can detect the "time of flight", or how long the light has taken to bounce back to the sensor. Since it uses a very narrow light source, it is good for determining distance of only the surface directly in front of it. Unlike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
  Esp32-c3 super mini: ESP32-C3 Development Board ESP32 SuperMini Development Board ESP32 Development Board WiFi Bluetooth.

// code stored in the sketch: BMP180_LCD_DHT22_SSD1306_VL6180.ino
/********************************************************************
SCL = A5
SDA = A4
GND = GND
OLED SSD1306 I2C= 5V
BMP180/085 I2C = 3.3 V!!!!!!!!!!!!!!!!
VL6180 I2C=3.3V!!!!!!!!!!!!!
DHT22=5V / data pin on digital 2
LCD I2C=5V
SDA/SCL Wired serial
---------------------------------------------------------
SDA (OLED)		SCL (OLED)		GND (OLED)	|
	|						|					|				|
	|						|					|				|
SDA (LCD)			SCL (LCD)		GND (LCD)		|
	|						|					|				|
	|						|					|				|
SDA BMP180		SCL BMP180	GND BMP180	|
	|						|					|				|
	|						|					|				|
SDA VL6180		SCL VL6180	GND VL6180	|
---------------------------------------------------------

VCC Wired individually. Not parallel or serial because of different Voltage! be carefull!!! 3.3V is not 5V!!!!!!

Adafruit_SSD1306 configured as 128x32!!! Doesnt matter if an 128x64 or 128x32 is attached!


********************************************************/
// Depends on the following Arduino libraries:
// - Adafruit Unified Sensor Library: https://github.com/adafruit/Adafruit_Sensor
// - DHT Sensor Library: https://github.com/adafruit/DHT-sensor-library
#include <Wire.h> 
#include <SPI.h>
#include <Adafruit_GFX.h>
#include <Adafruit_SSD1306.h>
#include "Adafruit_VL6180X.h"
#include <LiquidCrystal_I2C.h>
#include <Adafruit_Sensor.h>
#include <DHT.h>
#include <DHT_U.h>
#include <Adafruit_BMP085.h>
#define DHTPIN            2         // Pin which is connected to the DHT sensor.

// Uncomment the type of sensor in use:
//#define DHTTYPE           DHT11     // DHT 11 
#define DHTTYPE           DHT22     // DHT 22 (AM2302)
//#define DHTTYPE           DHT21     // DHT 21 (AM2301)

// See guide for details on sensor wiring and usage:
//   https://learn.adafruit.com/dht/overview
Adafruit_BMP085 bmp;
DHT_Unified dht(DHTPIN, DHTTYPE);
LiquidCrystal_I2C lcd(0x27, 16, 2);
Adafruit_VL6180X vl = Adafruit_VL6180X();
Adafruit_SSD1306 display = Adafruit_SSD1306();



uint32_t delayMS;

void setup() {
  Serial.begin(9600); 
    // initialize the LCD
  lcd.begin();
  display.begin(SSD1306_SWITCHCAPVCC, 0x3C);  // initialize with the I2C addr 0x3C (for the 128x32)
  // init done
  display.display();
  delay(1000);
    Serial.println("Adafruit VL6180x test!");
  if (! vl.begin()) {
    Serial.println("Failed to find sensor");
    while (1);
  }
  Serial.println("Sensor found!");

  // text display big!
  display.setTextSize(4);
  display.setTextColor(WHITE);
  
  // Turn on the blacklight and print a message.
  lcd.backlight();
    if (!bmp.begin()) {
  Serial.println("Could not find a valid BMP085 sensor, check wiring!");
  while (1) {}
  }
  // Initialize device.
  dht.begin();
  Serial.println("DHTxx Unified Sensor Example");
  // Print temperature sensor details.
  sensor_t sensor;
  dht.temperature().getSensor(&sensor);
  Serial.println("------------------------------------");
  Serial.println("Temperature");
  Serial.print  ("Sensor:       "); Serial.println(sensor.name);
  Serial.print  ("Driver Ver:   "); Serial.println(sensor.version);
  Serial.print  ("Unique ID:    "); Serial.println(sensor.sensor_id);
  Serial.print  ("Max Value:    "); Serial.print(sensor.max_value); Serial.println(" *C");
  Serial.print  ("Min Value:    "); Serial.print(sensor.min_value); Serial.println(" *C");
  Serial.print  ("Resolution:   "); Serial.print(sensor.resolution); Serial.println(" *C");  
  Serial.println("------------------------------------");
  // Print humidity sensor details.
  dht.humidity().getSensor(&sensor);
  Serial.println("------------------------------------");
  Serial.println("Humidity");
  Serial.print  ("Sensor:       "); Serial.println(sensor.name);
  Serial.print  ("Driver Ver:   "); Serial.println(sensor.version);
  Serial.print  ("Unique ID:    "); Serial.println(sensor.sensor_id);
  Serial.print  ("Max Value:    "); Serial.print(sensor.max_value); Serial.println("%");
  Serial.print  ("Min Value:    "); Serial.print(sensor.min_value); Serial.println("%");
  Serial.print  ("Resolution:   "); Serial.print(sensor.resolution); Serial.println("%");  
  Serial.println("------------------------------------");
  // Set delay between sensor readings based on sensor details.
  delayMS = sensor.min_delay / 1000;
}

void loop() {
  float lux = vl.readLux(VL6180X_ALS_GAIN_5);
    Serial.print("Lux: "); Serial.println(lux);
  
  uint8_t range = vl.readRange();
  uint8_t status = vl.readRangeStatus();

  if (status == VL6180X_ERROR_NONE) {
    Serial.print("Range: "); Serial.println(range);
    display.clearDisplay();
    display.setCursor(0,0);
    display.print(range);
    display.print("mm");
    display.display();
    Serial.println();
  } else {
    display.display();
    display.clearDisplay();
    return;
  }

  // Some error occurred, print it out!
  
  if  ((status >= VL6180X_ERROR_SYSERR_1) && (status <= VL6180X_ERROR_SYSERR_5)) {
    Serial.println("System error");
  }
  else if (status == VL6180X_ERROR_ECEFAIL) {
    Serial.println("ECE failure");
  }
  else if (status == VL6180X_ERROR_NOCONVERGE) {
    Serial.println("No convergence");
  }
  else if (status == VL6180X_ERROR_RANGEIGNORE) {
    Serial.println("Ignoring range");
  }
  else if (status == VL6180X_ERROR_SNR) {
    Serial.println("Signal/Noise error");
  }
  else if (status == VL6180X_ERROR_RAWUFLOW) {
    Serial.println("Raw reading underflow");
  }
  else if (status == VL6180X_ERROR_RAWOFLOW) {
    Serial.println("Raw reading overflow");
  }
  else if (status == VL6180X_ERROR_RANGEUFLOW) {
    Serial.println("Range reading underflow");
  }
  else if (status == VL6180X_ERROR_RANGEOFLOW) {
    Serial.println("Range reading overflow");
  }
  delay(10);
  // Delay between measurements.
  delay(delayMS);
  // Get temperature event and print its value.
  sensors_event_t event;  
  dht.temperature().getEvent(&event);
  if (isnan(event.temperature)) {
    Serial.println("Error reading temperature!");
  }
  else {
    Serial.print("Temperature: ");
    Serial.print(event.temperature);
    Serial.println(" *C");
  }
  // Get humidity event and print its value.
  dht.humidity().getEvent(&event);
  if (isnan(event.relative_humidity)) {
    Serial.println("Error reading humidity!");
  }
  else {
    Serial.print("Humidity: ");
    Serial.print(event.relative_humidity);
    Serial.println("%");
  }
      
    Serial.print("Temperature = ");
    Serial.print(bmp.readTemperature());
    Serial.println(" *C");
    
    Serial.print("Pressure = ");
    Serial.print(bmp.readPressure());
    Serial.println(" Pa");
    
    // Calculate altitude assuming 'standard' barometric
    // pressure of 1013.25 millibar = 101325 Pascal
    Serial.print("Altitude = ");
    Serial.print(bmp.readAltitude());
    Serial.println(" meters");

    Serial.print("Pressure at sealevel (calculated) = ");
    Serial.print(bmp.readSealevelPressure());
    Serial.println(" Pa");

  // you can get a more precise measurement of altitude
  // if you know the current sea level pressure which will
  // vary with weather and such. If it is 1015 millibars
  // that is equal to 101500 Pascals.
    Serial.print("Real altitude = ");
    Serial.print(bmp.readAltitude(101500));
    Serial.println(" meters");
    
    Serial.println();
    lcd.backlight();
    lcd.clear();
    lcd.setCursor(0,0);
    lcd.print("Lux:");
    lcd.setCursor(0,1);
    lcd.print(lux);
    delay(2000);
    lcd.clear();
    lcd.setCursor(0,0);
    lcd.print("Temperatur:(C)");
    lcd.setCursor(0,1);
    lcd.print(bmp.readTemperature());
    delay(2000);
    lcd.clear();
    lcd.setCursor(0,0);
    lcd.print("Temp (DHT22):(C)");
    lcd.setCursor(0,1);
    dht.temperature().getEvent(&event);
    lcd.print(event.temperature);
    delay(2000);
    lcd.clear();
    lcd.setCursor(0,0);
    lcd.print("Feuchtig: DHT22(%)");
    lcd.setCursor(0,1);
    dht.humidity().getEvent(&event);
    lcd.print(event.relative_humidity);
    delay(2000);
    lcd.clear();
    lcd.setCursor(0,0);
    lcd.print("Hoehe: (Meter)");
    lcd.setCursor(0,1);
    lcd.print(bmp.readAltitude(101500));
    delay(2000);
    lcd.clear();
    lcd.setCursor(0,0);
    lcd.print("Druck: (mBar)");
    lcd.setCursor(0,1);
    lcd.print(bmp.readPressure()/100);
    delay(1000);
}
